// Logisim project ex4.circ as structural Verilog: 1 circuit, main circuit my_scheme
module my_scheme (
  input  A,
  input  B,
  input  C,
  output Y
);

  wire and_1_out, and_2_out, NoA, NoB, NoC, not_4_out, or_1_out;

  not not_1 (NoA, A);
  not not_2 (NoB, B);
  not not_3 (NoC, C);
  and and_1 (and_1_out, NoA, NoB);
  and and_2 (and_2_out, NoA, B, NoC);
  or or_1 (or_1_out, A, NoC);
  not not_4 (not_4_out, or_1_out);
  or or_2 (Y, and_1_out, and_2_out, not_4_out);
endmodule
