// Logisim project ex5.circ as structural Verilog: 10 circuits, main circuit main
module main (
  input  [2:0] in_1,
  output [6:0] out_2
);

  wire decoder0_1_y, decoder0_1_y_1, decoder0_1_y_2, decoder0_1_y_3, decoder0_1_y_4, decoder0_1_y_5,
       decoder0_1_y_6, decoder0_1_y_7;
  wire [6:0] justneed_1_out_15;

  decoder0 decoder0_1 (
    .X_2(in_1[2]), .X_1(in_1[1]), .X_0(in_1[0]), .Y(decoder0_1_y), .Y_1(decoder0_1_y_1),
    .Y_2(decoder0_1_y_2), .Y_3(decoder0_1_y_3), .Y_4(decoder0_1_y_4), .Y_5(decoder0_1_y_5),
    .Y_6(decoder0_1_y_6), .Y_7(decoder0_1_y_7));
  JustNeed justneed_1 (
    .Y_7(decoder0_1_y), .Y_6(decoder0_1_y_1), .Y_5(decoder0_1_y_2), .Y_4(decoder0_1_y_3),
    .Y_3(decoder0_1_y_4), .Y_2(decoder0_1_y_5), .Y_1(decoder0_1_y_6), .Y(decoder0_1_y_7),
    .out_9(justneed_1_out_15[6]), .out_10(justneed_1_out_15[5]), .out_11(justneed_1_out_15[4]),
    .out_12(justneed_1_out_15[3]), .out_13(justneed_1_out_15[2]), .out_14(justneed_1_out_15[1]),
    .out_15(justneed_1_out_15[0]));
  assign out_2 = ~justneed_1_out_15;  // NOT_Gate not_1, 7 bits wide
endmodule

module decoder0 (
  input  X_2,
  input  X_1,
  input  X_0,
  output Y,
  output Y_1,
  output Y_2,
  output Y_3,
  output Y_4,
  output Y_5,
  output Y_6,
  output Y_7
);

  wire not_1_out, not_2_out, not_3_out;

  not not_1 (not_1_out, X_2);
  not not_2 (not_2_out, X_1);
  not not_3 (not_3_out, X_0);
  and and_1 (Y, not_3_out, not_2_out, not_1_out);
  and and_2 (Y_1, X_0, not_2_out, not_1_out);
  and and_3 (Y_2, not_3_out, X_1, not_1_out);
  and and_4 (Y_3, X_0, X_1, not_1_out);
  and and_5 (Y_4, not_3_out, not_2_out, X_2);
  and and_6 (Y_5, X_0, not_2_out, X_2);
  and and_7 (Y_6, not_3_out, X_1, X_2);
  and and_8 (Y_7, X_0, X_1, X_2);
endmodule

module JustNeed (
  input  Y_7,
  input  Y_6,
  input  Y_5,
  input  Y_4,
  input  Y_3,
  input  Y_2,
  input  Y_1,
  input  Y,
  output out_9,
  output out_10,
  output out_11,
  output out_12,
  output out_13,
  output out_14,
  output out_15
);

  OR7 or7_1 (.X(Y), .X_1(Y_1), .X_2(Y_2), .X_3(Y_3), .X_4(Y_4), .X_5(Y_5), .X_6(Y_6), .X_7(Y_7), .out_9(out_9));
  OR6 or6_1 (.X_1(Y_1), .X_2(Y_2), .X_3(Y_3), .X_4(Y_4), .X_5(Y_5), .X_6(Y_6), .X_7(Y_7), .out_8(out_10));
  OR5 or5_1 (.X_2(Y_2), .X_3(Y_3), .X_4(Y_4), .X_5(Y_5), .X_6(Y_6), .X_7(Y_7), .out_7(out_11));
  OR4 or4_1 (.X_3(Y_3), .X_4(Y_4), .X_5(Y_5), .X_6(Y_6), .X_7(Y_7), .out_6(out_12));
  OR3 or3_1 (.X_4(Y_4), .X_5(Y_5), .X_6(Y_6), .X_7(Y_7), .out_5(out_13));
  OR2 or2_1 (.X_5(Y_5), .X_6(Y_6), .X_7(Y_7), .out_4(out_14));
  ImplicationAnd implicationand_1 (.A(Y_6), .B(Y_7), .out_3(out_15));
endmodule

module ImplicationAnd (
  input  A,
  input  B,
  output out_3
);

  wire not_1_out, or_1_out;

  not not_1 (not_1_out, A);
  or or_1 (or_1_out, not_1_out, B);
  and and_1 (out_3, or_1_out, B);
endmodule

module OR7 (
  input  X,
  input  X_1,
  input  X_2,
  input  X_3,
  input  X_4,
  input  X_5,
  input  X_6,
  input  X_7,
  output out_9
);

  wire or_1_out;

  or or_1 (or_1_out, X_1, X_2, X_3, X_4, X_5, X_6, X_7);
  ImplicationAnd implicationand_1 (.A(X), .B(or_1_out), .out_3(out_9));
endmodule

module OR6 (
  input  X_1,
  input  X_2,
  input  X_3,
  input  X_4,
  input  X_5,
  input  X_6,
  input  X_7,
  output out_8
);

  wire or_1_out;

  or or_1 (or_1_out, X_2, X_3, X_4, X_5, X_6, X_7);
  ImplicationAnd implicationand_1 (.A(X_1), .B(or_1_out), .out_3(out_8));
endmodule

module OR5 (
  input  X_2,
  input  X_3,
  input  X_4,
  input  X_5,
  input  X_6,
  input  X_7,
  output out_7
);

  wire or_1_out;

  or or_1 (or_1_out, X_3, X_4, X_5, X_6, X_7);
  ImplicationAnd implicationand_1 (.A(X_2), .B(or_1_out), .out_3(out_7));
endmodule

module OR4 (
  input  X_3,
  input  X_4,
  input  X_5,
  input  X_6,
  input  X_7,
  output out_6
);

  wire or_1_out;

  or or_1 (or_1_out, X_4, X_5, X_6, X_7);
  ImplicationAnd implicationand_1 (.A(X_3), .B(or_1_out), .out_3(out_6));
endmodule

module OR3 (
  input  X_4,
  input  X_5,
  input  X_6,
  input  X_7,
  output out_5
);

  wire or_1_out;

  or or_1 (or_1_out, X_5, X_6, X_7);
  ImplicationAnd implicationand_1 (.A(X_4), .B(or_1_out), .out_3(out_5));
endmodule

module OR2 (
  input  X_5,
  input  X_6,
  input  X_7,
  output out_4
);

  wire or_1_out;

  or or_1 (or_1_out, X_6, X_7);
  ImplicationAnd implicationand_1 (.A(X_5), .B(or_1_out), .out_3(out_4));
endmodule
